// Digital circuit labtimer.dig as structural Verilog
module labtimer (
  input  CLK,
  input  SW,
  input  B3,
  input  B2,
  input  B1,
  input  B0,
  input  HZ1,
  output [3:0] M10,
  output [3:0] M1,
  output [3:0] S10,
  output [3:0] S1
);

  wire and_1_out, and_2_out, and_3_out, and_4_out, and_5_out, and_6_out, and_7_out, and_8_out, and_9_out,
       and_10_out, and_11_out, and_12_out, and_13_out, and_14_out, and_15_out, and_16_out, and_17_out,
       and_18_out, and_19_out, and_20_out, and_21_out, and_22_out, and_23_out, comparator_1_eq,
       comparator_2_eq, comparator_3_eq, comparator_4_eq, comparator_5_eq, comparator_6_eq, comparator_7_eq,
       comparator_8_eq, comparator_9_eq, comparator_10_eq, comparator_11_eq, comparator_12_eq,
       comparator_13_eq, comparator_14_eq, comparator_15_eq, comparator_16_eq, d_ff_1_q, d_ff_2_q, d_ff_3_q,
       d_ff_4_q, d_ff_5_nq, d_ff_5_q, not_1_out, not_2_out, not_3_out, not_4_out, not_5_out, not_6_out,
       or_1_out, or_2_out, or_3_out, or_4_out, or_5_out, register_5_q;
  wire [3:0] add_1_s, add_2_s, add_3_s, add_4_s, counter_1_out, counter_2_out, counter_3_out, counter_4_out,
       multiplexer_1_out, multiplexer_2_out, multiplexer_3_out, multiplexer_4_out, multiplexer_5_out,
       multiplexer_6_out, multiplexer_7_out, multiplexer_8_out, multiplexer_9_out, multiplexer_10_out,
       multiplexer_11_out, multiplexer_12_out, multiplexer_13_out, multiplexer_14_out, multiplexer_15_out,
       multiplexer_16_out, sub_1_s, sub_2_s, sub_3_s, sub_4_s;

  not not_1 (not_1_out, B3);
  not not_2 (not_2_out, B2);
  not not_3 (not_3_out, B1);
  not not_4 (not_4_out, B0);
  not not_5 (not_5_out, SW);
  D_FF d_ff_1 (.D(B3), .C(CLK), .Q(d_ff_1_q));  // open: nQ
  D_FF d_ff_2 (.D(B2), .C(CLK), .Q(d_ff_2_q));  // open: nQ
  D_FF d_ff_3 (.D(B1), .C(CLK), .Q(d_ff_3_q));  // open: nQ
  D_FF d_ff_4 (.D(B0), .C(CLK), .Q(d_ff_4_q));  // open: nQ
  and and_1 (and_1_out, not_5_out, HZ1);
  Add #(.Bits(4)) add_1 (.a(M10), .b(4'b0000), .c_i(and_17_out), .s(add_1_s));  // open: c_o
  Comparator #(.Bits(4)) comparator_1 (.a(M10), .b(4'b1001), .eq(comparator_1_eq));  // open: gt, lt
  and and_2 (and_2_out, d_ff_1_q, not_1_out);
  and and_3 (and_3_out, d_ff_2_q, not_2_out);
  and and_4 (and_4_out, d_ff_3_q, not_3_out);
  and and_5 (and_5_out, d_ff_4_q, not_4_out);
  and and_6 (and_6_out, and_17_out, comparator_1_eq, d_ff_5_q);
  or or_1 (or_1_out, and_6_out, and_15_out);
  and and_7 (and_7_out, SW, and_2_out);
  and and_8 (and_8_out, SW, and_3_out);
  and and_9 (and_9_out, SW, and_4_out);
  and and_10 (and_10_out, SW, and_5_out);
  Multiplexer #(.Bits(4)) multiplexer_1 (.sel(d_ff_5_q), .in_0(sub_1_s), .in_1(add_1_s), .out(multiplexer_1_out));
  Multiplexer #(.Bits(4)) multiplexer_2 (
    .sel(or_1_out), .in_0(multiplexer_1_out), .in_1(multiplexer_3_out), .out(multiplexer_2_out));
  Counter #(.Bits(4)) counter_1 (.en(and_7_out), .C(CLK), .clr(and_11_out), .out(counter_1_out));  // open: ovf
  Counter #(.Bits(4)) counter_2 (.en(and_8_out), .C(CLK), .clr(and_12_out), .out(counter_2_out));  // open: ovf
  Counter #(.Bits(4)) counter_3 (.en(and_9_out), .C(CLK), .clr(and_13_out), .out(counter_3_out));  // open: ovf
  Counter #(.Bits(4)) counter_4 (.en(and_10_out), .C(CLK), .clr(and_14_out), .out(counter_4_out));  // open: ovf
  Multiplexer #(.Bits(4)) multiplexer_3 (.sel(d_ff_5_q), .in_0(4'b1001), .in_1(4'b0000), .out(multiplexer_3_out));
  Comparator #(.Bits(4)) comparator_2 (.a(counter_1_out), .b(4'b1001), .eq(comparator_2_eq));  // open: gt, lt
  Comparator #(.Bits(4)) comparator_3 (.a(counter_2_out), .b(4'b1001), .eq(comparator_3_eq));  // open: gt, lt
  Comparator #(.Bits(4)) comparator_4 (.a(counter_3_out), .b(4'b0101), .eq(comparator_4_eq));  // open: gt, lt
  Comparator #(.Bits(4)) comparator_5 (.a(counter_4_out), .b(4'b1001), .eq(comparator_5_eq));  // open: gt, lt
  and and_11 (and_11_out, and_7_out, comparator_2_eq);
  and and_12 (and_12_out, and_8_out, comparator_3_eq);
  and and_13 (and_13_out, and_9_out, comparator_4_eq);
  and and_14 (and_14_out, and_10_out, comparator_5_eq);
  Multiplexer #(.Bits(4)) multiplexer_4 (
    .sel(SW), .in_0(multiplexer_2_out), .in_1(counter_1_out), .out(multiplexer_4_out));
  Register #(.Bits(4)) register_1 (.D(multiplexer_4_out), .C(CLK), .en(1'b1), .Q(M10));
  Sub #(.Bits(4)) sub_1 (.a(M10), .b(4'b0000), .c_i(and_16_out), .s(sub_1_s));  // open: c_o
  Comparator #(.Bits(4)) comparator_6 (.a(M10), .b(4'b0000), .eq(comparator_6_eq));  // open: gt, lt
  Comparator #(.Bits(4)) comparator_7 (.a(M10), .b(4'b0000), .eq(comparator_7_eq));  // open: gt, lt
  Multiplexer #(.Bits(4)) multiplexer_5 (
    .sel(SW), .in_0(multiplexer_8_out), .in_1(counter_2_out), .out(multiplexer_5_out));
  and and_15 (and_15_out, and_16_out, comparator_6_eq, d_ff_5_nq);
  Multiplexer #(.Bits(4)) multiplexer_6 (.sel(d_ff_5_q), .in_0(4'b1001), .in_1(4'b0000), .out(multiplexer_6_out));
  Register #(.Bits(4)) register_2 (.D(multiplexer_5_out), .C(CLK), .en(1'b1), .Q(M1));
  or or_2 (or_2_out, and_17_out, and_16_out);
  Sub #(.Bits(4)) sub_2 (.a(M1), .b(4'b0000), .c_i(and_19_out), .s(sub_2_s));  // open: c_o
  Comparator #(.Bits(4)) comparator_8 (.a(M1), .b(4'b0000), .eq(comparator_8_eq));  // open: gt, lt
  Add #(.Bits(4)) add_2 (.a(M1), .b(4'b0000), .c_i(and_20_out), .s(add_2_s));  // open: c_o
  Comparator #(.Bits(4)) comparator_9 (.a(M1), .b(4'b1001), .eq(comparator_9_eq));  // open: gt, lt
  Multiplexer #(.Bits(4)) multiplexer_7 (.sel(d_ff_5_q), .in_0(sub_2_s), .in_1(add_2_s), .out(multiplexer_7_out));
  Comparator #(.Bits(4)) comparator_10 (.a(M1), .b(4'b0000), .eq(comparator_10_eq));  // open: gt, lt
  and and_16 (and_16_out, and_19_out, comparator_8_eq, d_ff_5_nq);
  Multiplexer #(.Bits(4)) multiplexer_8 (
    .sel(or_2_out), .in_0(multiplexer_7_out), .in_1(multiplexer_6_out), .out(multiplexer_8_out));
  and and_17 (and_17_out, d_ff_5_q, comparator_9_eq, and_20_out);
  Multiplexer #(.Bits(4)) multiplexer_9 (.sel(d_ff_5_q), .in_0(4'b0101), .in_1(4'b0000), .out(multiplexer_9_out));
  Multiplexer #(.Bits(4)) multiplexer_10 (
    .sel(SW), .in_0(multiplexer_12_out), .in_1(counter_3_out), .out(multiplexer_10_out));
  Register #(.Bits(4)) register_3 (.D(multiplexer_10_out), .C(CLK), .en(1'b1), .Q(S10));
  Add #(.Bits(4)) add_3 (.a(S10), .b(4'b0000), .c_i(and_23_out), .s(add_3_s));  // open: c_o
  Sub #(.Bits(4)) sub_3 (.a(S10), .b(4'b0000), .c_i(and_22_out), .s(sub_3_s));  // open: c_o
  Comparator #(.Bits(4)) comparator_11 (.a(S10), .b(4'b0000), .eq(comparator_11_eq));  // open: gt, lt
  and and_18 (and_18_out, SW, not_4_out);
  Multiplexer #(.Bits(4)) multiplexer_11 (.sel(d_ff_5_q), .in_0(sub_3_s), .in_1(add_3_s), .out(multiplexer_11_out));
  Comparator #(.Bits(4)) comparator_12 (.a(S10), .b(4'b0101), .eq(comparator_12_eq));  // open: gt, lt
  or or_3 (or_3_out, and_20_out, and_19_out);
  Comparator #(.Bits(4)) comparator_13 (.a(S10), .b(4'b0000), .eq(comparator_13_eq));  // open: gt, lt
  or or_4 (or_4_out, and_18_out, and_1_out);
  and and_19 (and_19_out, and_22_out, comparator_11_eq, d_ff_5_nq);
  Multiplexer #(.Bits(4)) multiplexer_12 (
    .sel(or_3_out), .in_0(multiplexer_11_out), .in_1(multiplexer_9_out), .out(multiplexer_12_out));
  Multiplexer #(.Bits(4)) multiplexer_13 (
    .sel(SW), .in_0(multiplexer_16_out), .in_1(counter_4_out), .out(multiplexer_13_out));
  Register #(.Bits(4)) register_4 (.D(multiplexer_13_out), .C(CLK), .en(or_4_out), .Q(S1));
  and and_20 (and_20_out, and_23_out, comparator_12_eq, d_ff_5_q);
  Sub #(.Bits(4)) sub_4 (.a(S1), .b(4'b0001), .c_i(1'b0), .s(sub_4_s));  // open: c_o
  Add #(.Bits(4)) add_4 (.a(S1), .b(4'b0001), .c_i(1'b0), .s(add_4_s));  // open: c_o
  Comparator #(.Bits(4)) comparator_14 (.a(S1), .b(4'b0000), .eq(comparator_14_eq));  // open: gt, lt
  Comparator #(.Bits(4)) comparator_15 (.a(S1), .b(4'b0000), .eq(comparator_15_eq));  // open: gt, lt
  D_FF d_ff_5 (.D(register_5_q), .C(and_1_out), .Q(d_ff_5_q), .nQ(d_ff_5_nq));
  Comparator #(.Bits(4)) comparator_16 (.a(S1), .b(4'b1001), .eq(comparator_16_eq));  // open: gt, lt
  and and_21 (and_21_out, comparator_14_eq, comparator_13_eq, not_6_out, comparator_10_eq, comparator_7_eq);
  not not_6 (not_6_out, SW);
  and and_22 (and_22_out, comparator_15_eq, and_1_out, d_ff_5_nq);
  and and_23 (and_23_out, d_ff_5_q, comparator_16_eq, and_1_out);
  Multiplexer #(.Bits(4)) multiplexer_14 (.sel(d_ff_5_q), .in_0(4'b1001), .in_1(4'b0000), .out(multiplexer_14_out));
  Register register_5 (.D(and_21_out), .C(CLK), .en(and_21_out), .Q(register_5_q));
  Multiplexer #(.Bits(4)) multiplexer_15 (.sel(d_ff_5_q), .in_0(sub_4_s), .in_1(add_4_s), .out(multiplexer_15_out));
  Multiplexer #(.Bits(4)) multiplexer_16 (
    .sel(or_5_out), .in_0(multiplexer_15_out), .in_1(multiplexer_14_out), .out(multiplexer_16_out));
  or or_5 (or_5_out, and_22_out, and_23_out);

  // Notes on the sheet:
  //   SW: default 1
endmodule
